// Logisim project ALU.circ as structural Verilog: 1 circuit, main circuit ALU
module ALU (
  input  [31:0] A,
  input  [31:0] B,
  input  [4:0] Shift,
  input  [3:0] Codop,
  input  CarryIn,
  output [31:0] S,
  output [3:0] Flags
);

  wire CarryOut_ADC, CarryOut_CMN, CarryOut_CMP, CarryOut_SBC, comparator_2_eq;
  wire [31:0] multiplexer_1_out, not_1_out, sortie_ADC, sortie_AND, sortie_ASR, sortie_BIC, sortie_CMN,
       sortie_CMP, sortie_EOR, sortie_LSL, sortie_LSR, sortie_MUL, sortie_MVN, sortie_ORR, sortie_ROR,
       sortie_RSB, sortie_SBC, sortie_TST;

  Subtractor #(.width(32)) subtractor_1 (.a(B), .b(A), .out(sortie_CMP), .bout(CarryOut_CMP));  // open: bin
  Multiplier #(.width(32)) multiplier_1 (.a(A), .b(B), .out(sortie_MUL));  // open: cin, cout
  assign not_1_out = ~A;  // NOT_Gate not_1, 32 bits wide
  assign sortie_MVN = ~A;  // NOT_Gate not_2, 32 bits wide
  assign sortie_AND = A & B;  // AND_Gate and_1, 32 bits wide
  assign sortie_EOR = A ^ B;  // XOR_Gate xor_1, 32 bits wide
  Shifter #(.width(32)) shifter_1 (.in(B), .\dist (Shift), .out(sortie_LSL));
  Shifter #(.shift("lr"), .width(32)) shifter_2 (.in(B), .\dist (Shift), .out(sortie_LSR));
  Shifter #(.shift("ar"), .width(32)) shifter_3 (.in(B), .\dist (Shift), .out(sortie_ASR));
  Adder #(.width(32)) adder_1 (.a(A), .b(B), .out(sortie_ADC), .cin(CarryIn), .cout(CarryOut_ADC));
  Shifter #(.shift("rr"), .width(32)) shifter_4 (.in(B), .\dist (Shift), .out(sortie_ROR));
  assign sortie_TST = A & B;  // AND_Gate and_2, 32 bits wide
  Subtractor #(.width(32)) subtractor_2 (.a({32{1'b0}}), .b(A), .out(sortie_RSB));  // open: bin, bout
  Adder #(.width(32)) adder_2 (.a(A), .b(B), .out(sortie_CMN), .cout(CarryOut_CMN));  // open: cin
  assign sortie_ORR = A | B;  // OR_Gate or_1, 32 bits wide
  assign sortie_BIC = B & not_1_out;  // AND_Gate and_3, 32 bits wide
  Subtractor #(.width(32)) subtractor_3 (.a(A), .b(B), .out(sortie_SBC), .bin(CarryIn), .bout(CarryOut_SBC));
  Multiplexer #(.select(4), .width(32)) multiplexer_1 (
    .in0(sortie_AND), .in1(sortie_EOR), .in2(sortie_LSL), .in3(sortie_LSR), .in4(sortie_ASR),
    .in5(sortie_ADC), .in6(sortie_SBC), .in7(sortie_ROR), .in8(sortie_TST), .in9(sortie_RSB),
    .in10(sortie_CMP), .in11(sortie_CMN), .in12(sortie_ORR), .in13(sortie_MUL), .in14(sortie_BIC),
    .in15(sortie_MVN), .out(multiplexer_1_out), .sel(Codop));
  Multiplexer #(.select(4)) multiplexer_2 (
    .in0(1'b0), .in1(1'b0), .in2(1'b0), .in3(1'b0), .in4(1'b0), .in5(CarryOut_ADC), .in6(CarryOut_SBC),
    .in7(1'b0), .in8(1'b0), .in9(1'b0), .in10(CarryOut_CMP), .in11(CarryOut_CMN), .in12(1'b0), .in13(1'b0),
    .in14(1'b0), .in15(1'b0), .sel(Codop));  // open: out
  BitSelector #(.width(32)) bitselector_1 (.in(multiplexer_1_out), .out(Flags[3]), .sel({5{1'b1}}));
  Comparator #(.width(32)) comparator_1 (.a(multiplexer_1_out), .b({32{1'b0}}), .eq(Flags[2]));  // open: gt, lt
  Comparator #(.width(4)) comparator_2 (.a(Codop), .b(4'b1000), .eq(comparator_2_eq));  // open: gt, lt
  Multiplexer #(.width(32)) multiplexer_3 (.in0(multiplexer_1_out), .in1(B), .out(S), .sel(comparator_2_eq));

  // Other names for the same wires on the sheet: Cin = CarryIn; V = Flags[0]; C = Flags[1]; Z = Flags[2];
  //   N = Flags[3]

  // Notes on the sheet:
  //   Note: for ROR, C = N
  //   Note 2: assume that shift > 0 for LSL and LSR
endmodule
