// Logisim project Ctl_Data_Processing.circ as structural Verilog: 1 circuit, main circuit Data_Processing
module Data_Processing (
  input  Enable,
  input  [15:0] Instruction,
  output [2:0] Rd,
  output [2:0] Rn,
  output [2:0] Rm,
  output [3:0] ALU_Opcode,
  output [3:0] Flags_Update_Mask
);

  wire and_1_out;
  wire [2:0] Rm_t;
  wire [15:0] Flags_Update_Mask_t;

  // Multiplexer #(.width(4)) multiplexer_1: pin names not known; wires that end beside it: Instruction[9:6], Flags_Update_Mask_t[15:8]
  Multiplexer #(.width(3)) multiplexer_2 (.in0(Instruction[2:0]), .in1(Instruction[5:3]), .out(Rm_t), .sel(and_1_out));
  and and_1 (and_1_out, Instruction[6], ~Instruction[7], Instruction[8], Instruction[9]);  // AND_Gate
  and and_2 (Flags_Update_Mask_t[0], and_1_out, Instruction[8]);
  assign Rd = Enable ? ~Instruction[2:0] : 3'bz;  // Controlled_Inverter controlled_inverter_1
  assign Rn = Enable ? ~Rm_t : 3'bz;  // Controlled_Inverter controlled_inverter_2
  assign Rm = Enable ? ~Rm_t : 3'bz;  // Controlled_Inverter controlled_inverter_3
  assign ALU_Opcode = Enable ? ~Instruction[9:6] : 4'bz;  // Controlled_Inverter controlled_inverter_4
  assign Flags_Update_Mask = Enable ? ~Flags_Update_Mask_t[3:0] : 4'bz;  // Controlled_Inverter controlled_inverter_5
  // Pins of 3 and 4 and 16 bits meet at Flags_Update_Mask_t
  // Pins of 3 and 4 bits meet at Instruction[9:6]
  // Pins of 1 and 8 bits meet at Flags_Update_Mask_t[7:0]

  // Other names for the same wires on the sheet: Rd_t[2:0] = Instruction[2:0]; ALU_Opcode_t[3:0] = Instruction[9:6];
  //   Rn_t[2:0] = Rm_t

  // Notes on the sheet:
  //   Note 2: RSB instruction has Rn as 1st operand.
  //   MUL instruction has Rn as 1st operand and Rdm as 2nd operand
  //   For simplification purposes, Rm is used for 1st operand both here and in the ALU.
  //   Note: instructions that does not save the result will still have the second operand as the destination register, the ALU will copy the second register to the destination register
  //   Pull output low on Enable = 0
endmodule
