// Logisim project Ctl_Load_Store.circ as structural Verilog: 1 circuit, main circuit Load_Store
module Load_Store (
  input  [15:0] Instruction,
  input  Enable,
  input  Clk,
  input  Reset,
  input  [31:0] Stack_Pointer,
  output Store,
  output Load,
  output PC_Hold,
  output [2:0] Rmd,
  output [31:0] RAM_Addr
);

  wire Load_t, PC_Hold_t, Store_Load, Store_t;
  wire [2:0] Rmd_t;
  wire [31:0] RAM_Addr_t;

  BitSelector #(.width(16)) bitselector_1 (.in(Instruction), .out(Store_Load), .sel(4'b0000));
  Multiplexer multiplexer_1 (.in0(1'b0), .in1(Store_t), .out(Store), .sel(Enable));
  Multiplexer multiplexer_2 (.in0(1'b0), .in1(Load_t), .out(Load), .sel(Enable));
  Multiplexer multiplexer_3 (.in0(1'b0), .in1(PC_Hold_t), .out(PC_Hold), .sel(Enable));
  Multiplexer #(.width(3)) multiplexer_4 (.in0(3'b000), .in1(Rmd_t), .out(Rmd), .sel(Enable));
  Multiplexer #(.width(32)) multiplexer_5 (.in0({32{1'b0}}), .in1(RAM_Addr_t), .out(RAM_Addr), .sel(Enable));

  // Other names for the same wires on the sheet: CKL = Clk

  // Notes on the sheet:
  //   Instruction: pull=down
  //   Delay load and hold PC for 1 cycle for the RAM to send out requested data 
endmodule
