// Logisim project Ctl_Shift_Add_Sub_Mov.circ as structural Verilog: 1 circuit, main circuit Shift_Add_Sub_Mov
module Shift_Add_Sub_Mov (
  input  Enable,
  input  [15:0] Instruction,
  output [2:0] Rm,
  output [2:0] Rn,
  output [2:0] Rd,
  output [4:0] Imm5,
  output [3:0] Flags_Update_Mask,
  output [3:0] ALU_Opcode,
  output Imm32_Enable,
  output [31:0] Imm32,
  output Carry
);

  wire ADD3, ADDS, ADDS8, and_12_out, and_13_out, and_14_out, and_15_out, and_16_out, ASRS, CMPS, LSLS, LSRS,
       MOVS, or_9_out, or_12_out, or_13_out, Rd2_enable, Rd_enable, Rdn_enable, Rn_enable, SUB3, SUBS, SUBS8;
  wire [1:0] bit_extender_2_out;
  wire [2:0] Rd2_bis, Rd_bis, Rdn_bis, Rm2_bis, Rn_bis;
  wire [3:0] ALU, Flags, pull_resistor_1_node, pull_resistor_2_node, pull_resistor_3_node,
       pull_resistor_4_node, pull_resistor_5_node, pull_resistor_6_node, pull_resistor_7_node,
       pull_resistor_8_node, pull_resistor_9_node, pull_resistor_10_node, pull_resistor_11_node;
  wire [3:3] NZC, NZCV;
  wire [31:0] bit_extender_1_out, bit_extender_3_out, multiplexer_9_out, multiplexer_10_out, negator_1_out;

  assign ALU = pull_resistor_1_node | pull_resistor_2_node | pull_resistor_3_node | pull_resistor_4_node | pull_resistor_5_node | pull_resistor_6_node | pull_resistor_7_node | pull_resistor_8_node | pull_resistor_9_node | pull_resistor_10_node | pull_resistor_11_node;  // OR_Gate or_1, 4 bits wide
  and and_1 (ADDS, ~Instruction[9], ~Instruction[10], Instruction[11], Instruction[12], ~Instruction[13]);  // AND_Gate
  and and_2 (SUBS, Instruction[9], ~Instruction[10], Instruction[11], Instruction[12], ~Instruction[13]);  // AND_Gate
  and and_3 (ADD3, ~Instruction[9], Instruction[10], Instruction[11], Instruction[12], ~Instruction[13]);  // AND_Gate
  and and_4 (SUB3, Instruction[9], Instruction[10], Instruction[11], Instruction[12], ~Instruction[13]);  // AND_Gate
  and and_5 (LSLS, ~Instruction[11], ~Instruction[12], ~Instruction[13]);  // AND_Gate
  and and_6 (LSRS, Instruction[11], ~Instruction[12], ~Instruction[13]);  // AND_Gate
  and and_7 (ASRS, ~Instruction[11], Instruction[12], ~Instruction[13]);  // AND_Gate
  and and_8 (MOVS, ~Instruction[11], ~Instruction[12], Instruction[13]);  // AND_Gate
  and and_9 (CMPS, Instruction[11], ~Instruction[12], Instruction[13]);  // AND_Gate
  and and_10 (ADDS8, ~Instruction[11], Instruction[12], Instruction[13]);  // AND_Gate
  and and_11 (SUBS8, Instruction[11], Instruction[12], Instruction[13]);
  or or_2 (NZCV[3], SUBS8, SUBS, SUB3, CMPS, ADD3, ADDS, ADDS8);
  or or_3 (NZC[3], LSLS, ASRS, LSRS);
  Pull_Resistor pull_resistor_1 (.node(pull_resistor_1_node));
  assign pull_resistor_1_node = ADDS ? 4'b0101 : 4'bz;  // Controlled_Buffer controlled_buffer_1
  Pull_Resistor pull_resistor_2 (.node(pull_resistor_2_node));
  assign pull_resistor_2_node = SUBS ? 4'b0110 : 4'bz;  // Controlled_Buffer controlled_buffer_2
  Pull_Resistor pull_resistor_3 (.node(pull_resistor_3_node));
  assign pull_resistor_3_node = ADD3 ? 4'b0101 : 4'bz;  // Controlled_Buffer controlled_buffer_3
  Pull_Resistor pull_resistor_4 (.node(pull_resistor_4_node));
  assign pull_resistor_4_node = SUB3 ? 4'b0110 : 4'bz;  // Controlled_Buffer controlled_buffer_4
  Pull_Resistor pull_resistor_5 (.node(pull_resistor_5_node));
  assign pull_resistor_5_node = LSRS ? 4'b0011 : 4'bz;  // Controlled_Buffer controlled_buffer_5
  Pull_Resistor pull_resistor_6 (.node(pull_resistor_6_node));
  assign pull_resistor_6_node = LSLS ? 4'b0010 : 4'bz;  // Controlled_Buffer controlled_buffer_6
  Pull_Resistor pull_resistor_7 (.node(pull_resistor_7_node));
  assign pull_resistor_7_node = ASRS ? 4'b0100 : 4'bz;  // Controlled_Buffer controlled_buffer_7
  Pull_Resistor pull_resistor_8 (.node(pull_resistor_8_node));
  assign pull_resistor_8_node = CMPS ? 4'b1010 : 4'bz;  // Controlled_Buffer controlled_buffer_8
  Pull_Resistor pull_resistor_9 (.node(pull_resistor_9_node));
  assign pull_resistor_9_node = ADDS8 ? 4'b0101 : 4'bz;  // Controlled_Buffer controlled_buffer_9
  Pull_Resistor pull_resistor_10 (.node(pull_resistor_10_node));
  assign pull_resistor_10_node = MOVS ? 4'b1001 : 4'bz;  // Controlled_Buffer controlled_buffer_10
  Pull_Resistor pull_resistor_11 (.node(pull_resistor_11_node));
  assign pull_resistor_11_node = SUBS8 ? 4'b0110 : 4'bz;  // Controlled_Buffer controlled_buffer_11
  assign Flags = {4{NZCV[3]}} | {{3{NZC[3]}}, 1'b0} | {{2{MOVS}}, 2'b00};  // OR_Gate or_4, 4 bits wide
  or or_5 (Rn_enable, ADDS, SUBS, ADD3, SUB3);
  or or_6 (Rdn_enable, MOVS, CMPS, ADDS8, SUBS8);
  or or_7 (Rd2_enable, LSLS, LSRS, ASRS);
  or or_8 (Rd_enable, SUB3, SUBS, ADD3, ADDS);
  and and_12 (and_12_out, Rd2_enable, Enable);
  and and_13 (and_13_out, Rdn_enable, Enable);
  and and_14 (and_14_out, Rd2_enable, Enable);
  Multiplexer #(.width(3)) multiplexer_1 (.in0(3'b000), .in1(Instruction[2:0]), .out(Rd2_bis), .sel(and_12_out));
  Multiplexer #(.width(3)) multiplexer_2 (.in0(3'b000), .in1(Instruction[10:8]), .out(Rdn_bis), .sel(and_13_out));
  Multiplexer #(.width(3)) multiplexer_3 (.in0(3'b000), .in1(Instruction[5:3]), .out(Rm2_bis), .sel(and_14_out));
  Multiplexer #(.width(3)) multiplexer_4 (.in0(3'b000), .in1(Instruction[2:0]), .out(Rd_bis), .sel(and_15_out));
  and and_15 (and_15_out, Rd_enable, Enable);
  Multiplexer #(.width(3)) multiplexer_5 (.in0(3'b000), .in1(Instruction[5:3]), .out(Rn_bis), .sel(and_16_out));
  and and_16 (and_16_out, Rn_enable, Enable);
  assign Imm32_Enable = Enable ? or_9_out : 1'bz;  // Controlled_Buffer controlled_buffer_12
  Pull_Resistor pull_resistor_12 (.node(Imm32_Enable));
  assign bit_extender_1_out = {{24{1'b0}}, Instruction[7:0]};  // Bit_Extender bit_extender_1
  assign bit_extender_2_out = {{1{1'b0}}, Enable};  // Bit_Extender bit_extender_2
  assign ALU_Opcode = Enable ? ALU : 4'bz;  // Controlled_Buffer controlled_buffer_13
  Pull_Resistor pull_resistor_13 (.node(ALU_Opcode));
  or or_9 (or_9_out, MOVS, CMPS, ADDS8, SUBS8, or_12_out);
  Negator #(.width(32)) negator_1 (.in(bit_extender_1_out), .out(negator_1_out));
  Multiplexer #(.select(2), .width(3)) multiplexer_6 (
    .in0(3'b000), .in1(Instruction[8:6]), .in2(Instruction[5:3]), .in3(Instruction[8:6]), .out(Rm),
    .sel(bit_extender_2_out));
  assign Rn = Rdn_bis | Rn_bis | Rm2_bis;  // OR_Gate or_10, 3 bits wide
  assign Rd = Rdn_bis | Rd2_bis | Rd_bis;  // OR_Gate or_11, 3 bits wide
  Multiplexer #(.width(5)) multiplexer_7 (.in0({5{1'b0}}), .in1(Instruction[10:6]), .out(Imm5), .sel(Enable));
  Multiplexer #(.width(4)) multiplexer_8 (.in0(4'b0000), .in1(Flags), .out(Flags_Update_Mask), .sel(Enable));
  or or_12 (or_12_out, ADD3, SUB3);
  assign bit_extender_3_out = {{29{1'b0}}, Instruction[8:6]};  // Bit_Extender bit_extender_3
  Multiplexer #(.width(32)) multiplexer_9 (
    .in0(bit_extender_1_out), .in1(negator_1_out), .out(multiplexer_9_out), .sel(MOVS));
  or or_13 (or_13_out, SUBS8, SUBS, SUB3);
  Multiplexer #(.width(32)) multiplexer_10 (
    .in0(bit_extender_3_out), .in1(multiplexer_9_out), .out(multiplexer_10_out), .sel(Instruction[13]));
  Pull_Resistor pull_resistor_14 (.node(Carry));
  assign Carry = Enable ? or_13_out : 1'bz;  // Controlled_Buffer controlled_buffer_14
  assign Imm32 = Enable ? multiplexer_10_out : 32'bz;  // Controlled_Buffer controlled_buffer_15
  Pull_Resistor pull_resistor_15 (.node(Imm32));

  // Other names for the same wires on the sheet: imm8[7:0] = Instruction[7:0]; Rd2[2:0] = Instruction[2:0];
  //   Rd_t[2:0] = Instruction[2:0]; Rm2[2:0] = Instruction[5:3]; Rn_t[2:0] = Instruction[5:3];
  //   imm3[2:0] = Instruction[8:6]; imm5_t[4:0] = Instruction[10:6]; Rm_t[2:0] = Instruction[8:6];
  //   Rdn[2:0] = Instruction[10:8]; opcode[4:0] = Instruction[13:9]; opcode2[2:0] = Instruction[13:11];
  //   opcode3[2:0] = Instruction[13:11]; b13 = Instruction[13]; NZ[3:2] = {2{MOVS}}; NZC[2:1] = {2{NZC[3]}};
  //   NZCV[2:0] = {3{NZCV[3]}}

  // Notes on the sheet:
  //   Note 3: Imm32_Enable forces the use of the immediate for Rm register
  //   Pull output low on Enable = 0
  //   when imm3, imm32 is enabled
  //   Note: ALU uses Rn register for shifts. Use Rn instead of Rm for shifts (immediate) here too
  //   Enable carry for SUB since it is reversed in ALU
  //   ALU will use Imm32 instead of Rm
  //   only ADD and SUB use Rm
  //   Note 2: MOV uses RSB ALU opcode with Imm8 reversed so that it is copied to output register
endmodule
